# Fritzing sketch lcm1602-i2c-leds (saved by Fritzing 0.9.6b)
breadboards: 1

parts:
  Part1 = Arduino Mega 2560 (Rev3)
  LCM1602_IIC3 = LCM1602 IIC [part_number="LCM1602 IIC" chip_label="LCM1602 IIC" package="DIP (Dual Inline) [THT]"]
  LED1 = LED - 5mm [color="Red (633nm)" current=0.030 package="5 mm [THT]"]
  R1 = Resistor [tolerance=±5% power=0.25 resistance=220 package=THT]
  LED2 = LED - 5mm [color="Red (633nm)" current=0.030 package="5 mm [THT]"]
  R2 = Resistor [tolerance=±5% power=0.25 resistance=220 package=THT]
  LED3 = LED - 5mm [color="Red (633nm)" current=0.030 package="5 mm [THT]"]
  LED4 = LED - 5mm [color="Red (633nm)" current=0.030 package="5 mm [THT]"]
  LED5 = LED - 5mm [color="Red (633nm)" current=0.030 package="5 mm [THT]"]
  LED6 = LED - 5mm [color="Red (633nm)" current=0.030 package="5 mm [THT]"]
  LED7 = LED - 5mm [color="Red (633nm)" current=0.030 package="5 mm [THT]"]
  LED8 = LED - 5mm [color="Red (633nm)" current=0.030 package="5 mm [THT]"]
  R3 = Resistor [tolerance=±5% power=0.25 resistance=220 package=THT]
  R4 = Resistor [tolerance=±5% power=0.25 resistance=220 package=THT]
  R5 = Resistor [tolerance=±5% power=0.25 resistance=220 package=THT]
  R6 = Resistor [tolerance=±5% power=0.25 resistance=220 package=THT]
  R7 = Resistor [tolerance=±5% power=0.25 resistance=220 package=THT]
  R8 = Resistor [tolerance=±5% power=0.25 resistance=220 package=THT]

nets:
  N1: Part1.D21/SCL, LCM1602_IIC3.SCL
  N2: Part1.D20/SDA, LCM1602_IIC3.SDA
  5V: Part1.5V, LCM1602_IIC3.VCC, R1.Pin_0, R2.Pin_0, R3.Pin_0, R4.Pin_0, R5.Pin_0, R6.Pin_0, R7.Pin_0, R8.Pin_0
  GND: Part1.GND, LCM1602_IIC3.GND
  N3: LCM1602_IIC3.D0, LED8.cathode
  N4: LCM1602_IIC3.D1, LED7.cathode
  N5: LCM1602_IIC3.D2, LED6.cathode
  N6: LCM1602_IIC3.D3, LED5.cathode
  N7: LCM1602_IIC3.D4, LED4.cathode
  N8: LCM1602_IIC3.D5, LED3.cathode
  N9: LCM1602_IIC3.D6, LED2.cathode
  N10: LCM1602_IIC3.D7, LED1.cathode
  N11: LED1.anode, R1.Pin_1
  N12: LED2.anode, R2.Pin_1
  N13: LED3.anode, R3.Pin_1
  N14: LED4.anode, R4.Pin_1
  N15: LED5.anode, R5.Pin_1
  N16: LED6.anode, R6.Pin_1
  N17: LED7.anode, R7.Pin_1
  N18: LED8.anode, R8.Pin_1

custom parts:
  LCM1602 IIC: I2C-Module to use a 1602 or 2004 LCD on with the wire.h libory Serial LCD Modul
